# Fritzing sketch Termometro (saved by Fritzing 0.9.9b)
breadboards: 1

parts:
  Componente1 = Arduino Uno (Rev3)
  DHT1 = DHT11 Humitidy and Temperature Sensor
  LCD1 = LCD screen
  R1 = Rotary Potentiometer (Small) [maximum_resistance=100kΩ package=THT]
  LED1 = LED - 5mm [color="Red (633nm)" current=0.030 package="5 mm [THT]"]
  LED2 = LED - 5mm [color="Green (555nm)" current=0.030 package="5 mm [THT]"]
  LED3 = LED - 5mm [color="Blue (505nm)" current=0.030 package="5 mm [THT]"]
  R2 = Resistor [tolerance=±5% power=0.25 resistance=220 package=THT]
  R3 = Resistor [tolerance=±5% power=0.25 resistance=220 package=THT]
  R4 = Resistor [tolerance=±5% power=0.25 resistance=220 package=THT]

nets:
  N1: Componente1.D8, LCD1.E
  N2: Componente1.D9_PWM, LCD1.DB4
  N3: Componente1.D10_PWM/SS, LCD1.DB5
  N4: Componente1.D11_PWM/MOSI, LCD1.DB6
  N5: Componente1.D12/MISO, LCD1.DB7
  N6: Componente1.D2, DHT1.NULL
  N7: Componente1.D3_PWM, R4.Pin_0
  N8: Componente1.D5_PWM, R3.Pin_0
  N9: Componente1.D6_PWM, R2.Pin_0
  N10: Componente1.D7, LCD1.RS
  VDD: DHT1.VDD, LCD1.VSS, LCD1.R/W, LCD1.LED-, R1.leg2
  N11: DHT1.DATA, LCD1.VDD, LCD1.LED+, R1.leg1
  N12: LCD1.V0, R1.wiper
  N13: LED1.cathode, LED2.cathode, LED3.cathode
  N14: LED1.anode, R2.Pin_1
  N15: LED2.anode, R3.Pin_1
  N16: LED3.anode, R4.Pin_1

custom parts:
  DHT11 Humitidy and Temperature Sensor: DHT11 Humidity and Temperature Sensor
